# Fritzing sketch fritzing (saved by Fritzing 0.9.10b)
breadboards: 1

parts:
  M1 = DC Motor [voltage_(max)=6V voltage_(min)=3V]
  M2 = DC Motor [voltage_(max)=6V voltage_(min)=3V]
  IC1 = L293D [package=THT]
  VCC1 = Battery block 9V
  CUI-enc1 = AMT103
  CUI-enc2 = AMT103
  S1 = Pololu QTR-8 Reflectabce Sensor array [package=THT]
  Part1 = Arduino Uno (Rev3)
  S2 = SWITCH-MOMENTARY-2 [package=tactile_switch_tall]

nets:
  N1: M1.pin_1, IC1.Out_1_(_Controlled_by_Enable_1_)
  N2: M1.pin_2, IC1.Out_2_(_Controlled_by_Enable_1_)
  N3: M2.pin_1, IC1.Out_4_(_Controlled_by_Enable_2_)
  N4: M2.pin_2, IC1.Out_3_(_Controlled_by_Enable_2_)
  N5: IC1.Enable_1, Part1.D5_PWM
  N6: IC1.In_1, Part1.D6_PWM
  GND: IC1.0V, VCC1.+, CUI-enc1.GND, CUI-enc2.GND, S1.pin15, Part1.GND, S2.1
  N7: IC1.In_2, Part1.D7
  N8: IC1.+Vmotor, VCC1.-
  N9: IC1.Enable_2, Part1.D11_PWM/MOSI
  N10: IC1.In_3, Part1.D10_PWM/SS
  N11: IC1.In_4, Part1.D9_PWM
  5V: IC1.+V, CUI-enc1.5V, CUI-enc2.5V, S1.pin13, S1.pin14, S1.pin23
  N12: CUI-enc1.B, Part1.D13/SCK
  N13: CUI-enc1.A, Part1.D2
  N14: CUI-enc2.B, Part1.D3_PWM
  N15: CUI-enc2.A, Part1.D4
  N16: S1.pin6, Part1.A0
  N17: S1.pin7, Part1.A1
  N18: S1.pin8, Part1.A2
  N19: S1.pin9, Part1.A3
  N20: S1.pin10, Part1.A4/SDA
  N21: S1.pin11, Part1.A5/SCL
  N22: Part1.D8, S2.2
